# Fritzing sketch RFID RC522 (saved by Fritzing 1.0.3b)
breadboards: 3

parts:
  Part1 = RFID-RC522-v2
  LCD2 = LCD screen
  DHT1 = DHT11 Humitidy and Temperature Sensor (3 pins)
  M1 = ESP32-S2-DevKitC-1 [part_number=ESP32-S2-DevKitC-1]
  VCC1 = Battery block 9V [internal_resistance=0.1Ω]
  U1 = LM2596 step down module
  C2 = Electrolytic Capacitor [capacitance=1pF voltage=50V package="200 mil [THT, electrolytic]"]
  C3 = Electrolytic Capacitor [capacitance=100µF voltage=50V package="200 mil [THT, electrolytic]"]
  LED1 = LED - 3mm [color="Red (633nm)" current=0.030A package="3 mm [THT]"]
  LED2 = LED - 3mm [color="Blue (525nm)" current=0.030A package="3 mm [THT]"]
  LED3 = LED - 3mm [color="Orange (620nm)" current=0.030A package="3 mm [THT]"]
  S1 = Pushbutton [package="[THT]"]
  S2 = Pushbutton [package="[THT]"]
  R1 = Resistor [tolerance=±5% power=0.25W resistance=220 package=THT]
  R2 = Resistor [tolerance=±5% power=0.25W resistance=220 package=THT]
  R3 = Resistor [tolerance=±5% power=0.25W resistance=220 package=THT]
  R4 = Resistor [tolerance=±5% power=0.25W resistance=220 package=THT]
  R5 = Resistor [tolerance=±5% power=0.25W resistance=220 package=THT]
  LCM1602_IIC2 = LCM1602 IIC [part_number="LCM1602 IIC" chip_label="LCM1602 IIC" package="DIP (Dual Inline) [THT]"]
  SG2 = Buzzer 12mm [part_number=COM-07950 package=buzzer-12mm-ns]
  Part2 = Adafruit PN532 NFC RFID Controller Shield [part_number="Adafruit #789"]  # not connected
  Part3 = PN532 Elechouse RFID NFC Module V3  # not connected

nets:
  N1: Part1.SDA, S1.Pin_3, S1.Pin_4, S2.Pin_3, S2.Pin_4
  N2: Part1.SCK, M1.pin_38
  N3: Part1.MOSI, VCC1.-, U1.IN-, U1.OUT-, C2.+, C3.+, R1.Pin_1, R2.Pin_1
  N4: Part1.IRQ, M1.pin_34
  N5: Part1.GND, M1.pin_32
  N6: Part1.RST, M1.pin_33
  N7: Part1.3.3V, M1.pin_17
  VSS: LCD2.VSS, LCM1602_IIC2.VSS
  VDD: LCD2.VDD, LCM1602_IIC2.VDD
  N8: LCD2.V0, LCM1602_IIC2.V0
  N9: LCD2.RS, LCM1602_IIC2.RS
  N10: LCD2.R/W, LCM1602_IIC2.RW
  N11: LCD2.E, LCM1602_IIC2.E
  N12: LCD2.DB0, LCM1602_IIC2.D0
  N13: LCD2.DB1, LCM1602_IIC2.D1
  N14: LCD2.DB2, LCM1602_IIC2.D2
  N15: LCD2.DB3, LCM1602_IIC2.D3
  N16: LCD2.DB4, LCM1602_IIC2.D4
  N17: LCD2.DB5, LCM1602_IIC2.D5
  N18: LCD2.DB6, LCM1602_IIC2.D6
  N19: LCD2.DB7, LCM1602_IIC2.D7
  N20: LCD2.LED+, LCM1602_IIC2.A
  N21: LCD2.LED-, LCM1602_IIC2.K
  N22: DHT1.Plus, M1.pin_14
  N23: DHT1.Signal, M1.pin_21, LCM1602_IIC2.VCC
  GND: DHT1.Gnd, U1.OUT+, C3.-, LCM1602_IIC2.GND
  N24: M1.pin_1, M1.pin_2, R3.Pin_1, R4.Pin_1, R5.Pin_1, SG2.2
  N25: M1.pin_8, LED2.cathode
  N26: M1.pin_9, SG2.1
  N27: M1.pin_10, LED3.cathode
  N28: M1.pin_12, LCM1602_IIC2.SDA
  N29: M1.pin_15, LCM1602_IIC2.SCL
  N30: M1.pin_22, M1.pin_23, M1.pin_24, M1.pin_44, LED1.cathode
  N31: M1.pin_39, S2.Pin_1, S2.Pin_2, R1.Pin_0
  N32: M1.pin_40, S1.Pin_1, S1.Pin_2, R2.Pin_0
  N33: VCC1.+, U1.IN+, C2.-
  N34: LED1.anode, R3.Pin_0
  N35: LED2.anode, R4.Pin_0
  N36: LED3.anode, R5.Pin_0

notes:
  The pins on the RFID reader are very important and shouldn't be changed.
  The buzzer currently runs on the 3.3v of the GPIO pins resulting in a muted sound.
  The mini DCDC Converter, converts the batteries 9V to a 5v for powering the ESP32, DHT11 and the LCD display
  The capacitors ensure stable and smooth input and output voltage
  Buttons for selecting modes and increase and decrease
  Orange = Scanned
  Blue = Wifi Connection
  Red = Power
  DHT sensor for monitoring Internal Temperatures
  LCD uses an I2C backpack to minimize pin usage

custom parts:
  RFID-RC522-v2: A simple China made RFID-RC522 Reader; do check the pin labels, as this is a MFRC522 based clone.
  DHT11 Humitidy and Temperature Sensor (3 pins): DHT11 Humidity and Temperature Sensor (3 pins).
  ESP32-S2-DevKitC-1: ESP32-S2-DevKitC-1 is an entry-level development board based on ESP32-S2-SOLO (on-board PCB antenna). It is based on the ESP32 microcontroller that boasts Wifi, Bluetooth, Ethernet and Low Power support all in a single chip. (vanepp) Feb 2022: converted to ESP32-S2-DevKitC-1. This module is 44pins long (2x22) and 11 pins width.
  LM2596 step down module: LM2596 DC-DC step down power supply module 3 A.
  LCM1602 IIC: I2C-Module to use a 1602 or 2004 LCD on with the wire.h libory Serial LCD Modul
  Buzzer 12mm: Buzzer 12mm Spark Fun Electronics SKU : Comp-Buzzer Through hole This is a small 12mm round speaker that operates around the audible 2kHz range. You can use these speakers to create simple music or user interfaces. This is not a true piezoelectric speaker but behaves similarly. Instead of a piezoelectric crystal that vibrates with an electric current, this tiny speaker uses an electromagnet to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
  Adafruit PN532 NFC RFID Controller Shield: We've taken our popular Adafruit PN532 breakout board and turned it into a shield - the perfect tool for any 13.56MHz RFID or NFC application. The Adafruit NFC shield uses the PN532 chip-set (the most popular NFC chip on the market) and is what is embedded in pretty much every phone or device that does NFC. This chipset is very powerful, and can pretty much do it all, such as read and write to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
  PN532 Elechouse RFID NFC Module V3: NFC is a popular technology in recent years. We often heard this work while smart phone company such as Samsung or HTC introduces their latest high-end phones. Almost all the high-end phone in the market support NFC. Near field communication (NFC) is a set of standards for smart phones and similar devices to establish radio communication with each other by touching them together or bringing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
