# Fritzing sketch RFID RC522 (saved by Fritzing 1.0.3b)
breadboards: 1

parts:
  M1 = ESP32-S2-DevKitC-1 [part_number=ESP32-S2-DevKitC-1]
  SG2 = Buzzer 12mm [part_number=COM-07950 package=buzzer-12mm-ns]
  LED2 = LED - 5mm [color="Red (633nm)" current=0.030 package="5 mm [THT]"]
  RFID_Scanner = RFID-RC522-v2
  R2 = Resistor [tolerance=±5% power=0.25 resistance=220 package=THT]

nets:
  N1: M1.pin_1, M1.pin_2, RFID_Scanner.3.3V
  N2: M1.pin_5, SG2.2
  N3: M1.pin_9, RFID_Scanner.GND
  N4: M1.pin_14, RFID_Scanner.SDA
  N5: M1.pin_22, M1.pin_23, M1.pin_24, M1.pin_44, SG2.1, RFID_Scanner.RST, R2.Pin_1
  N6: M1.pin_32, RFID_Scanner.SCK
  N7: M1.pin_33, RFID_Scanner.MOSI
  N8: M1.pin_34, RFID_Scanner.MISO
  N9: M1.pin_39, LED2.cathode
  N10: LED2.anode, R2.Pin_0

notes:
  The pins on the RFID reader are very important and shouldn't be changed.
  The buzzer currnelty runs on the 3.3v of the GPIO pins resulting in a muted sound.
  It could be possible using a transistor to power it to 5v from the 5v pin on the ESP32.

custom parts:
  ESP32-S2-DevKitC-1: ESP32-S2-DevKitC-1 is an entry-level development board based on ESP32-S2-SOLO (on-board PCB antenna). It is based on the ESP32 microcontroller that boasts Wifi, Bluetooth, Ethernet and Low Power support all in a single chip. (vanepp) Feb 2022: converted to ESP32-S2-DevKitC-1. This module is 44pins long (2x22) and 11 pins width.
  Buzzer 12mm: Buzzer 12mm Spark Fun Electronics SKU : Comp-Buzzer Through hole This is a small 12mm round speaker that operates around the audible 2kHz range. You can use these speakers to create simple music or user interfaces. This is not a true piezoelectric speaker but behaves similarly. Instead of a piezoelectric crystal that vibrates with an electric current, this tiny speaker uses an electromagnet to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
  RFID-RC522-v2: A simple China made RFID-RC522 Reader; do check the pin labels, as this is a MFRC522 based clone.
